# Fritzing sketch Circuit (saved by Fritzing 0.9.3b)
breadboards: 1

parts:
  R1 = Resistor [tolerance=±5% resistance=2.2k package="0603 [SMD]"]
  D1 = LTE-302 [package=lte-302]
  Part2 = Arduino Uno (Rev3)
  Q1 = NPN-Transistor [package="TO92 [THT]"]
  IR1 = TSOP312.., 314.. [package=THT]
  Part3 = Bluetooth HC-05 Macho

nets:
  N1: R1.Pin_0, Q1.B
  N2: R1.Pin_1, Part2.D3_PWM
  N3: D1.A, Q1.E
  GND: D1.C, Part2.GND, IR1.GND, Part3.GND
  N4: Part2.D11_PWM/MOSI, IR1.Data
  N5: Part2.D0/RX, Part3.TXD
  N6: Part2.D1/TX, Part3.RXD
  5V: Part2.5V, Q1.C, IR1.Vs, Part3.VCC
